// Logisim project parcial.circ as structural Verilog: 5 circuits, main circuit fsm
module fsm (
  input  B2,
  input  B1,
  output S22,
  output S11,
  output S00
);

  wire and_1_out, and_2_out, and_3_out, and_4_out, and_5_out, and_6_out, and_7_out, and_8_out, and_9_out,
       and_10_out, and_11_out, clock_1_out, d_ff_1_q, d_ff_2_q, d_ff_3_q, not_1_out, not_2_out, not_3_out,
       not_4_out, not_5_out, not_6_out, not_7_out, not_8_out, not_9_out, not_10_out, not_11_out, not_12_out,
       not_13_out, not_14_out, not_15_out, not_16_out, not_17_out, not_18_out, not_19_out, not_20_out,
       not_21_out, not_22_out;

  not not_1 (not_1_out, d_ff_1_q);
  not not_2 (not_2_out, d_ff_3_q);
  not not_3 (not_3_out, d_ff_1_q);
  not not_4 (not_4_out, d_ff_1_q);
  not not_5 (not_5_out, d_ff_2_q);
  not not_6 (not_6_out, d_ff_3_q);
  not not_7 (not_7_out, d_ff_1_q);
  not not_8 (not_8_out, d_ff_2_q);
  not not_9 (not_9_out, B1);
  not not_10 (not_10_out, d_ff_1_q);
  not not_11 (not_11_out, B2);
  not not_12 (not_12_out, B1);
  not not_13 (not_13_out, d_ff_2_q);
  not not_14 (not_14_out, d_ff_3_q);
  not not_15 (not_15_out, B1);
  not not_16 (not_16_out, d_ff_2_q);
  not not_17 (not_17_out, d_ff_3_q);
  not not_18 (not_18_out, B2);
  not not_19 (not_19_out, d_ff_1_q);
  not not_20 (not_20_out, B2);
  not not_21 (not_21_out, d_ff_1_q);
  not not_22 (not_22_out, d_ff_2_q);
  and and_1 (and_1_out, not_1_out, d_ff_2_q, not_2_out);
  and and_2 (and_2_out, not_3_out, d_ff_2_q, B1);
  and and_3 (and_3_out, not_4_out, d_ff_2_q, B2);
  and and_4 (and_4_out, d_ff_1_q, not_5_out, not_6_out, B1);
  and and_5 (and_5_out, not_7_out, not_8_out, B2, not_9_out);
  and and_6 (and_6_out, not_10_out, d_ff_2_q, d_ff_3_q, not_11_out, not_12_out);
  and and_7 (and_7_out, d_ff_1_q, not_13_out, not_14_out, not_15_out);
  and and_8 (and_8_out, not_16_out, not_17_out, not_18_out, B1);
  and and_9 (and_9_out, not_19_out, d_ff_2_q, d_ff_3_q, not_20_out);
  and and_10 (and_10_out, not_21_out, d_ff_2_q, d_ff_3_q, B1);
  and and_11 (and_11_out, d_ff_1_q, not_22_out);
  or or_1 (S22, and_1_out, and_2_out, and_3_out, and_4_out);
  or or_2 (S11, and_5_out, and_6_out, and_7_out);
  or or_3 (S00, and_8_out, and_9_out, and_10_out, and_11_out);
  Clock clock_1 (.out(clock_1_out));
  D_Flip_Flop d_ff_1 (.clk(clock_1_out), .D(S22), .Q(d_ff_1_q));  // open: Qn, preset, en, reset
  D_Flip_Flop d_ff_2 (.clk(clock_1_out), .D(S11), .Q(d_ff_2_q));  // open: Qn, preset, en, reset
  D_Flip_Flop d_ff_3 (.clk(clock_1_out), .D(S00), .Q(d_ff_3_q));  // open: Qn, preset, en, reset
endmodule

module main (
  input  Call_2,
  input  Call_PB
);

  wire actions_1_d, actions_1_door, actions_1_u, fsm_1_s00, fsm_1_s11, fsm_1_s22, indicator_1_downarrow,
       indicator_1_i1, indicator_1_i2, indicator_1_uparrow, output_1_c0, output_1_c1;

  Indicator indicator_1 (
    .S2(fsm_1_s22), .S1(fsm_1_s11), .S0(fsm_1_s00), .I1(indicator_1_i1), .I2(indicator_1_i2),
    .DownArrow(indicator_1_downarrow), .UpArrow(indicator_1_uparrow));
  fsm fsm_1 (.B2(Call_2), .B1(Call_PB), .S22(fsm_1_s22), .S11(fsm_1_s11), .S00(fsm_1_s00));
  LED led_1 (.in(indicator_1_i2));
  LED led_2 (.in(indicator_1_i1));
  \output  output_1 (.S2(fsm_1_s22), .S1(fsm_1_s11), .S0(fsm_1_s00), .C1(output_1_c1), .C0(output_1_c0));
  LED led_3 (.in(indicator_1_downarrow));
  LED led_4 (.in(indicator_1_uparrow));
  actions actions_1 (.C1(output_1_c1), .C0(output_1_c0), .D(actions_1_d), .U(actions_1_u), .Door(actions_1_door));
  LED led_5 (.in(actions_1_d));
  LED led_6 (.in(actions_1_u));
  LED led_7 (.in(actions_1_door));

  // Notes on the sheet:
  //   Indicator Logic
  //   State Logic
  //   2
  //   1
  //   Output Logic
  //   ↓
  //   ↑
  //   Action logic
  //   Elevador Bajando
  //   Elevador Subiendo
  //   Abrir puertas y cerrar
endmodule

module \output  (
  input  S2,
  input  S1,
  input  S0,
  output C1,
  output C0
);

  wire and_1_out, and_2_out, and_3_out, and_4_out, and_5_out, not_1_out, not_2_out, not_3_out, not_4_out,
       not_5_out, not_6_out, not_7_out, not_8_out;

  not not_1 (not_1_out, S1);
  not not_2 (not_2_out, S1);
  not not_3 (not_3_out, S2);
  not not_4 (not_4_out, S1);
  not not_5 (not_5_out, S2);
  not not_6 (not_6_out, S0);
  not not_7 (not_7_out, S1);
  not not_8 (not_8_out, S0);
  and and_1 (and_1_out, not_1_out, S0);
  and and_2 (and_2_out, S2, not_2_out);
  and and_3 (and_3_out, not_3_out, not_4_out, S0);
  and and_4 (and_4_out, not_5_out, S1, not_6_out);
  and and_5 (and_5_out, S2, not_7_out, not_8_out);
  or or_1 (C1, and_1_out, and_2_out);
  or or_2 (C0, and_3_out, and_4_out, and_5_out);
endmodule

module actions (
  input  C1,
  input  C0,
  output D,
  output U,
  output Door
);

  wire not_1_out, not_2_out;

  not not_1 (not_1_out, C0);
  not not_2 (not_2_out, C1);
  and and_1 (Door, C1, C0);
  and and_2 (D, C1, not_1_out);
  and and_3 (U, not_2_out, C0);
endmodule

module Indicator (
  input  S2,
  input  S1,
  input  S0,
  output I1,
  output I2,
  output DownArrow,
  output UpArrow
);

  wire and_2_out, and_3_out, not_1_out, not_2_out, not_3_out, not_4_out, not_5_out, not_6_out, not_7_out,
       not_8_out;

  not not_1 (not_1_out, S2);
  not not_2 (not_2_out, S1);
  not not_3 (not_3_out, S2);
  not not_4 (not_4_out, S1);
  not not_5 (not_5_out, S0);
  not not_6 (not_6_out, S1);
  not not_7 (not_7_out, S2);
  not not_8 (not_8_out, S0);
  and and_1 (I1, not_1_out, not_2_out);
  and and_2 (and_2_out, not_3_out, S1, S0);
  and and_3 (and_3_out, S2, not_4_out, not_5_out);
  and and_4 (DownArrow, S2, not_6_out, S0);
  and and_5 (UpArrow, not_7_out, S1, not_8_out);
  or or_1 (I2, and_2_out, and_3_out);
endmodule
